# Fritzing sketch TM-garden (saved by Fritzing 0.9.4)
breadboards: 1

parts:
  KY-1 = Keyes Relay [package=THT]
  Parça1 = Arduino Nano (Rev3.0)
  J1 = Power Jack [package=power_jack_combo]
  X2 = USB Connectors [package=usb-a-s-silk-female]
  M1 = DC Motor
  Parça2 = NeoPixel Stick [part_number=1426]
  R1 = Photocell (LDR) [package=THT]
  R2 = Resistor [tolerance=±5% resistance=10k package=THT]
  Parça3 = Soil Moisture Sensor

nets:
  N1: KY-1.signal, Parça1.D5
  5V: KY-1.power, Parça1.5V, R1.pin_0, Parça3.VCC
  GND: KY-1.ground, Parça1.GND, J1.GND, X2.GND, M1.pin_1, Parça2.GND, R2.Pin_0, Parça3.GND
  N2: KY-1.NC, M1.pin_2
  N3: KY-1.C, X2.VBUS, Parça2.+5V
  N4: Parça1.D7, Parça2.DATAIN
  N5: Parça1.VIN, J1.PWR
  N6: Parça1.A2, Parça3.SIG
  N7: Parça1.A0, R1.pin_1, R2.Pin_1

custom parts:
  Keyes Relay: The Keyes 5V relay module is suitable for SCM development, home appliance control. It uses a 5V~12V TIL control signal which can control DC / AC signal.
  NeoPixel Stick: Make your own little LED strip arrangement with this stick of NeoPixel LEDs. We crammed 8 of the tiny 5050 (5mm x 5mm) smart RGB LEDs onto a PCB with mounting holes and a chainable design. Use only one microcontroller pin to control as many as you can chain together! Each LED is addressable as the driver chip is inside the LED. Each one has ~18mA constant current drive so the color will be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
